# Fritzing sketch diagram (saved by Fritzing 1.0.5)

parts:
  PWM1 = PCA9685 16x12-bit PWM Breakout
  Part1 = Arduino Uno (Rev3) - ICSP
  J1 = Basic Servo
  J2 = Basic Servo
  J3 = Basic Servo
  J4 = Basic Servo
  PWM2 = PCA9685 16x12-bit PWM Breakout
  JACK1 = 2.1mm Barrel Jack with Terminal Block
  JACK2 = 2.1mm Barrel Jack with Terminal Block

nets:
  N1: PWM1.no_name_yet#0, J1.pulse
  N2: PWM1.no_name_yet#1, J2.pulse
  N3: PWM1.no_name_yet#2, J3.pulse
  N4: PWM1.no_name_yet#3, J4.pulse
  N5: PWM1.no_name_yet#100, PWM1.no_name_yet#101, PWM1.no_name_yet#102, PWM1.no_name_yet#103, PWM1.no_name_yet#606, PWM1.no_name_yet#706, PWM2.no_name_yet#506, PWM2.no_name_yet#706, JACK1.POS, JACK2.POS
  N6: PWM1.no_name_yet#501, PWM1.no_name_yet#601, PWM1.no_name_yet#701, PWM1.no_name_yet#1000, PWM1.no_name_yet#1001, PWM1.no_name_yet#1002, PWM1.no_name_yet#1003, Part1.GND, PWM2.no_name_yet#501, PWM2.no_name_yet#701, JACK1.NEG, JACK2.NEG
  N7: PWM1.no_name_yet#503, PWM1.no_name_yet#603, Part1.A5/SCL, PWM2.no_name_yet#503
  N8: PWM1.no_name_yet#504, PWM1.no_name_yet#604, Part1.A4/SDA, PWM2.no_name_yet#504
  N9: PWM1.no_name_yet#505, PWM1.no_name_yet#605, Part1.5V, PWM2.no_name_yet#505
  N10: PWM1.no_name_yet#602, PWM2.no_name_yet#502
